# Fritzing sketch enter (saved by Fritzing 0.9.3b)
breadboards: 1

parts:
  パーツ1 = Arduino Uno (Rev3)
  LED1 = LED - 5mm [color="Yellow (595nm)" package="5 mm [THT]"]
  LED2 = LED - 5mm [color="Yellow (595nm)" package="5 mm [THT]"]
  R1 = Resistor [tolerance=±5% resistance=47 package=THT]
  LED3 = LED - 5mm [color="White (4500K)" package="5 mm [THT]"]
  LED4 = LED - 5mm [color="White (4500K)" package="5 mm [THT]"]
  R2 = Resistor [tolerance=±5% resistance=47 package=THT]
  LED5 = LED - 5mm [color="Red (633nm)" package="5 mm [THT]"]
  LED6 = LED - 5mm [color="Red (633nm)" package="5 mm [THT]"]
  R3 = Resistor [tolerance=±5% resistance=47 package=THT]
  LED7 = LED - 5mm [color="Green (565nm)" package="5 mm [THT]"]
  LED8 = LED - 5mm [color="Green (570nm)" package="5 mm [THT]"]
  R4 = Resistor [tolerance=±5% resistance=47 package=THT]
  J3 = Infrared Proximity Sensor
  J4 = Piezo Speaker

nets:
  N1: パーツ1.A0, J3.Vout
  N2: パーツ1.D8, J4.pin2
  N3: パーツ1.GND, LED1.cathode, LED2.cathode, LED5.cathode, LED6.cathode, LED7.cathode, LED8.cathode, J4.pin1
  N4: パーツ1.D7, R1.Pin_0, LED3.cathode, LED4.cathode, R2.Pin_0, R4.Pin_0
  5V: パーツ1.5V, J3.Vcc
  N5: LED1.anode, LED2.anode, R1.Pin_1
  N6: LED3.anode, LED4.anode, R2.Pin_1
  N7: LED5.anode, LED6.anode, R3.Pin_1
  N8: LED7.anode, LED8.anode, R4.Pin_1
